# Fritzing sketch Sensorlog (saved by Fritzing 0.9.2b)
breadboards: 1

parts:
  Часть1 = Arduino Uno (Rev3)
  VCC1 = Battery block 9V  # not connected
  LED1 = LED - 5mm [color="Red (633nm)" package="5 mm [THT]"]
  RHT1 = Humidity and Temperature Sensor RHT03
  U1 = GAS_SENSOR [package=mq-3]
  Часть2 = Bluetooth Mate Silver
  R1 = Resistor [tolerance=±5% resistance=220 package=THT]
  U3 = GAS_SENSOR [package=mq-3]
  U4 = GAS_SENSOR [package=mq-3]
  Часть3 = Breakout Board for Electret Microphone

nets:
  N1: Часть1.D13/SCK, LED1.anode
  GND: Часть1.GND, LED1.cathode, RHT1.GND_2, U1.A1, Часть2.TX_5V, U3.B1, U4.B1, Часть3.GND
  N2: Часть1.D0/RX, Часть2.CTS_5V
  N3: Часть1.D1/TX, Часть2.VCC
  N4: Часть1.D2, RHT1.GND_1, R1.Pin_0
  N5: Часть1.D5_PWM, Часть3.VCC
  5V: Часть1.5V, RHT1.Vcc, U1.B1, Часть2.RX_5V, R1.Pin_1, U3.A1, U4.A1, Часть3.AUD

notes:
  mq-2
  Bluetooth
  DHT11
  mq-7
  mq-4
  FC-04
